// Logisim project proj_1.circ as structural Verilog: 4 circuits, main circuit main
module main (
);

  wire clock_1_out, dec_7seg_driver_1_a, dec_7seg_driver_1_b, dec_7seg_driver_1_c, dec_7seg_driver_1_d,
       dec_7seg_driver_1_e, dec_7seg_driver_1_f, dec_7seg_driver_1_g, dec_counter_1__0, dec_counter_1__1,
       dec_counter_1__2, dec_counter_1__3;

  Clock clock_1 (.out(clock_1_out));
  dec_counter dec_counter_1 (
    .Clock(clock_1_out), ._0(dec_counter_1__0), ._1(dec_counter_1__1), ._2(dec_counter_1__2),
    ._3(dec_counter_1__3));  // open: RESET
  dec_7seg_driver dec_7seg_driver_1 (
    .w(dec_counter_1__0), .x(dec_counter_1__1), .y(dec_counter_1__2), .z(dec_counter_1__3),
    .b(dec_7seg_driver_1_b), .a(dec_7seg_driver_1_a), .f(dec_7seg_driver_1_f), .g(dec_7seg_driver_1_g),
    .e(dec_7seg_driver_1_e), .d(dec_7seg_driver_1_d), .c(dec_7seg_driver_1_c));
  _7_Segment_Display u_7_segment_display_1 (
    .g(dec_7seg_driver_1_g), .f(dec_7seg_driver_1_f), .a(dec_7seg_driver_1_a), .b(dec_7seg_driver_1_b),
    .e(dec_7seg_driver_1_e), .d(dec_7seg_driver_1_d), .c(dec_7seg_driver_1_c));  // open: dp
endmodule

module bonus (
);

  wire clock_1_out, dec_7seg_driver_1_a, dec_7seg_driver_1_b, dec_7seg_driver_1_c, dec_7seg_driver_1_d,
       dec_7seg_driver_1_e, dec_7seg_driver_1_f, dec_7seg_driver_1_g, dec_7seg_driver_2_a,
       dec_7seg_driver_2_b, dec_7seg_driver_2_c, dec_7seg_driver_2_d, dec_7seg_driver_2_e,
       dec_7seg_driver_2_f, dec_7seg_driver_2_g, dec_counter_1__0, dec_counter_1__1, dec_counter_1__2,
       dec_counter_1__3, dec_counter_1_reset, dec_counter_2__0, dec_counter_2__1, dec_counter_2__2,
       dec_counter_2__3;

  Clock clock_1 (.out(clock_1_out));
  dec_counter dec_counter_1 (
    .Clock(clock_1_out), .RESET(dec_counter_1_reset), ._0(dec_counter_1__0), ._1(dec_counter_1__1),
    ._2(dec_counter_1__2), ._3(dec_counter_1__3));
  dec_counter dec_counter_2 (
    .Clock(dec_counter_1_reset), ._0(dec_counter_2__0), ._1(dec_counter_2__1), ._2(dec_counter_2__2),
    ._3(dec_counter_2__3));  // open: RESET
  dec_7seg_driver dec_7seg_driver_1 (
    .w(dec_counter_1__0), .x(dec_counter_1__1), .y(dec_counter_1__2), .z(dec_counter_1__3),
    .b(dec_7seg_driver_1_b), .a(dec_7seg_driver_1_a), .f(dec_7seg_driver_1_f), .g(dec_7seg_driver_1_g),
    .e(dec_7seg_driver_1_e), .d(dec_7seg_driver_1_d), .c(dec_7seg_driver_1_c));
  dec_7seg_driver dec_7seg_driver_2 (
    .w(dec_counter_2__0), .x(dec_counter_2__1), .y(dec_counter_2__2), .z(dec_counter_2__3),
    .b(dec_7seg_driver_2_b), .a(dec_7seg_driver_2_a), .f(dec_7seg_driver_2_f), .g(dec_7seg_driver_2_g),
    .e(dec_7seg_driver_2_e), .d(dec_7seg_driver_2_d), .c(dec_7seg_driver_2_c));
  _7_Segment_Display u_7_segment_display_1 (
    .g(dec_7seg_driver_2_g), .f(dec_7seg_driver_2_f), .a(dec_7seg_driver_2_a), .b(dec_7seg_driver_2_b),
    .e(dec_7seg_driver_2_e), .d(dec_7seg_driver_2_d), .c(dec_7seg_driver_2_c));  // open: dp
  _7_Segment_Display u_7_segment_display_2 (
    .g(dec_7seg_driver_1_g), .f(dec_7seg_driver_1_f), .a(dec_7seg_driver_1_a), .b(dec_7seg_driver_1_b),
    .e(dec_7seg_driver_1_e), .d(dec_7seg_driver_1_d), .c(dec_7seg_driver_1_c));  // open: dp
endmodule

module dec_counter (
  input  Clock,
  output _0,
  output _1,
  output _2,
  output _3,
  output RESET
);

  wire and_2_out, and_3_out, and_4_out, and_5_out, and_6_out, and_7_out, and_8_out, D1_qn, D2_qn, D3_qn,
       D4_qn, or_1_out, or_2_out, or_3_out;

  and and_1 (RESET, _3, D2_qn, D3_qn, _0);
  and and_2 (and_2_out, _3, D4_qn);
  and and_3 (and_3_out, _2, _1, _0);
  and and_4 (and_4_out, _2, D3_qn);
  and and_5 (and_5_out, _2, D4_qn);
  and and_6 (and_6_out, D2_qn, _1, _0);
  and and_7 (and_7_out, _1, D4_qn);
  and and_8 (and_8_out, D1_qn, D3_qn, _0);
  or or_1 (or_1_out, and_2_out, and_3_out);
  or or_2 (or_2_out, and_4_out, and_5_out, and_6_out);
  or or_3 (or_3_out, and_7_out, and_8_out);
  D_Flip_Flop #(.trigger("falling")) D1 (.clk(Clock), .D(or_1_out), .Q(_3), .Qn(D1_qn));  // open: preset, en, reset
  D_Flip_Flop #(.trigger("falling")) D2 (.clk(Clock), .D(or_2_out), .Q(_2), .Qn(D2_qn));  // open: preset, en, reset
  D_Flip_Flop #(.trigger("falling")) D3 (.clk(Clock), .D(or_3_out), .Q(_1), .Qn(D3_qn));  // open: preset, en, reset
  D_Flip_Flop #(.trigger("falling")) D4 (.clk(Clock), .D(D4_qn), .Q(_0), .Qn(D4_qn));  // open: preset, en, reset
endmodule

module dec_7seg_driver (
  input  w,
  input  x,
  input  y,
  input  z,
  output b,
  output a,
  output f,
  output g,
  output e,
  output d,
  output c
);

  wire and_1_out, and_2_out, and_3_out, and_4_out, and_5_out, and_6_out, and_7_out, and_8_out, and_9_out,
       and_10_out, and_11_out, and_12_out, and_13_out, and_14_out, and_15_out, and_16_out, not_1_out,
       not_2_out, not_3_out;

  not not_1 (not_1_out, w);
  not not_2 (not_2_out, x);
  not not_3 (not_3_out, y);
  and and_1 (and_1_out, not_1_out, not_2_out);
  and and_2 (and_2_out, w, x);
  and and_3 (and_3_out, not_1_out, not_3_out);
  and and_4 (and_4_out, w, y);
  and and_5 (and_5_out, not_1_out, not_2_out);
  and and_6 (and_6_out, not_2_out, y);
  and and_7 (and_7_out, not_1_out, y);
  and and_8 (and_8_out, not_3_out, x);
  and and_9 (and_9_out, not_1_out, y);
  and and_10 (and_10_out, not_2_out, y);
  and and_11 (and_11_out, not_1_out, not_3_out);
  and and_12 (and_12_out, not_1_out, x);
  and and_13 (and_13_out, not_1_out, not_3_out);
  and and_14 (and_14_out, w, not_2_out, y);
  and and_15 (and_15_out, not_3_out, x);
  and and_16 (and_16_out, x, not_1_out);
  or or_1 (c, w, not_2_out, y);
  or or_2 (b, and_1_out, not_3_out, and_2_out);
  or or_3 (a, and_3_out, x, z, and_4_out);
  or or_4 (f, and_5_out, and_6_out, and_7_out, z);
  or or_5 (g, and_8_out, and_9_out, and_10_out, z);
  or or_6 (e, and_11_out, and_12_out);
  or or_7 (d, and_13_out, and_14_out, z, and_15_out, and_16_out);
  _7_Segment_Display u_7_segment_display_1 (.g(g), .f(f), .a(a), .b(b), .e(e), .d(d), .c(c));  // open: dp
endmodule
