// Logisim project proj_2.circ as structural Verilog: 7 circuits, main circuit main
module main (
  input  in_1,
  input  in_2,
  input  in_3,
  input  in_4,
  input  in_5,
  input  in_6,
  input  in_7,
  input  in_8
);

  wire dec_7seg_driver_1_a, dec_7seg_driver_1_b, dec_7seg_driver_1_c, dec_7seg_driver_1_d,
       dec_7seg_driver_1_e, dec_7seg_driver_1_f, dec_7seg_driver_1_g, dec_7seg_driver_2_a,
       dec_7seg_driver_2_b, dec_7seg_driver_2_c, dec_7seg_driver_2_d, dec_7seg_driver_2_e,
       dec_7seg_driver_2_f, dec_7seg_driver_2_g, dec_7seg_driver_3_a, dec_7seg_driver_3_b,
       dec_7seg_driver_3_c, dec_7seg_driver_3_d, dec_7seg_driver_3_e, dec_7seg_driver_3_f,
       dec_7seg_driver_3_g, dec_7seg_driver_4_a, dec_7seg_driver_4_b, dec_7seg_driver_4_c,
       dec_7seg_driver_4_d, dec_7seg_driver_4_e, dec_7seg_driver_4_f, dec_7seg_driver_4_g,
       n4bit_to_out_1_out_5, n4bit_to_out_1_out_6, n4bit_to_out_1_out_7, n4bit_to_out_1_out_8,
       n4bit_to_out_1_out_9, n4bit_to_out_1_out_10, n4bit_to_out_1_out_11, n4bit_to_out_1_out_12,
       n4bitadder_1_p9, n4bitadder_1_p10, n4bitadder_1_p11, n4bitadder_1_p12;

  _7_Segment_Display u_7_segment_display_1 (
    .g(dec_7seg_driver_1_g), .f(dec_7seg_driver_1_f), .a(dec_7seg_driver_1_a), .b(dec_7seg_driver_1_b),
    .e(dec_7seg_driver_1_e), .d(dec_7seg_driver_1_d), .c(dec_7seg_driver_1_c));  // open: dp
  dec_7seg_driver dec_7seg_driver_1 (
    .w(in_4), .x(in_3), .y(in_2), .z(in_1), .b(dec_7seg_driver_1_b), .a(dec_7seg_driver_1_a),
    .f(dec_7seg_driver_1_f), .g(dec_7seg_driver_1_g), .e(dec_7seg_driver_1_e), .d(dec_7seg_driver_1_d),
    .c(dec_7seg_driver_1_c));
  dec_7seg_driver dec_7seg_driver_2 (
    .w(in_8), .x(in_7), .y(in_6), .z(in_5), .b(dec_7seg_driver_2_b), .a(dec_7seg_driver_2_a),
    .f(dec_7seg_driver_2_f), .g(dec_7seg_driver_2_g), .e(dec_7seg_driver_2_e), .d(dec_7seg_driver_2_d),
    .c(dec_7seg_driver_2_c));
  _4bit_to_out u_4bit_to_out_1 (
    .in_1(n4bitadder_1_p9), .in_2(n4bitadder_1_p10), .in_3(n4bitadder_1_p11), .in_4(n4bitadder_1_p12),
    .out_5(n4bit_to_out_1_out_5), .out_6(n4bit_to_out_1_out_6), .out_7(n4bit_to_out_1_out_7),
    .out_8(n4bit_to_out_1_out_8), .out_9(n4bit_to_out_1_out_9), .out_10(n4bit_to_out_1_out_10),
    .out_11(n4bit_to_out_1_out_11), .out_12(n4bit_to_out_1_out_12));
  // _4bitadder 4bitadder_1: pin names not known; wires that end beside it: in_8, in_7, in_6, in_5, in_4, in_3, in_2, in_1, n4bitadder_1_p9, n4bitadder_1_p10, n4bitadder_1_p11, n4bitadder_1_p12
  dec_7seg_driver dec_7seg_driver_3 (
    .w(n4bit_to_out_1_out_5), .x(n4bit_to_out_1_out_6), .y(n4bit_to_out_1_out_7), .z(n4bit_to_out_1_out_8),
    .b(dec_7seg_driver_3_b), .a(dec_7seg_driver_3_a), .f(dec_7seg_driver_3_f), .g(dec_7seg_driver_3_g),
    .e(dec_7seg_driver_3_e), .d(dec_7seg_driver_3_d), .c(dec_7seg_driver_3_c));
  dec_7seg_driver dec_7seg_driver_4 (
    .w(n4bit_to_out_1_out_9), .x(n4bit_to_out_1_out_10), .y(n4bit_to_out_1_out_11),
    .z(n4bit_to_out_1_out_12), .b(dec_7seg_driver_4_b), .a(dec_7seg_driver_4_a), .f(dec_7seg_driver_4_f),
    .g(dec_7seg_driver_4_g), .e(dec_7seg_driver_4_e), .d(dec_7seg_driver_4_d), .c(dec_7seg_driver_4_c));
  _7_Segment_Display u_7_segment_display_2 (
    .g(dec_7seg_driver_2_g), .f(dec_7seg_driver_2_f), .a(dec_7seg_driver_2_a), .b(dec_7seg_driver_2_b),
    .e(dec_7seg_driver_2_e), .d(dec_7seg_driver_2_d), .c(dec_7seg_driver_2_c));  // open: dp
  _7_Segment_Display u_7_segment_display_3 (
    .g(dec_7seg_driver_3_g), .f(dec_7seg_driver_3_f), .a(dec_7seg_driver_3_a), .b(dec_7seg_driver_3_b),
    .e(dec_7seg_driver_3_e), .d(dec_7seg_driver_3_d), .c(dec_7seg_driver_3_c));  // open: dp
  _7_Segment_Display u_7_segment_display_4 (
    .g(dec_7seg_driver_4_g), .f(dec_7seg_driver_4_f), .a(dec_7seg_driver_4_a), .b(dec_7seg_driver_4_b),
    .e(dec_7seg_driver_4_e), .d(dec_7seg_driver_4_d), .c(dec_7seg_driver_4_c));  // open: dp

  // Notes on the sheet:
  //   +
  //   =
endmodule

module dec_counter (
  input  Clock,
  output _0,
  output _1,
  output _2,
  output _3,
  output RESET
);

  wire and_2_out, and_3_out, and_4_out, and_5_out, and_6_out, and_7_out, and_8_out, D1_qn, D2_qn, D3_qn,
       D4_qn, or_1_out, or_2_out, or_3_out;

  and and_1 (RESET, _3, D2_qn, D3_qn, _0);
  and and_2 (and_2_out, _3, D4_qn);
  and and_3 (and_3_out, _2, _1, _0);
  and and_4 (and_4_out, _2, D3_qn);
  and and_5 (and_5_out, _2, D4_qn);
  and and_6 (and_6_out, D2_qn, _1, _0);
  and and_7 (and_7_out, _1, D4_qn);
  and and_8 (and_8_out, D1_qn, D3_qn, _0);
  or or_1 (or_1_out, and_2_out, and_3_out);
  or or_2 (or_2_out, and_4_out, and_5_out, and_6_out);
  or or_3 (or_3_out, and_7_out, and_8_out);
  D_Flip_Flop #(.trigger("falling")) D1 (.clk(Clock), .D(or_1_out), .Q(_3), .Qn(D1_qn));  // open: preset, en, reset
  D_Flip_Flop #(.trigger("falling")) D2 (.clk(Clock), .D(or_2_out), .Q(_2), .Qn(D2_qn));  // open: preset, en, reset
  D_Flip_Flop #(.trigger("falling")) D3 (.clk(Clock), .D(or_3_out), .Q(_1), .Qn(D3_qn));  // open: preset, en, reset
  D_Flip_Flop #(.trigger("falling")) D4 (.clk(Clock), .D(D4_qn), .Q(_0), .Qn(D4_qn));  // open: preset, en, reset
endmodule

module dec_7seg_driver (
  input  w,
  input  x,
  input  y,
  input  z,
  output b,
  output a,
  output f,
  output g,
  output e,
  output d,
  output c
);

  wire and_1_out, and_2_out, and_3_out, and_4_out, and_5_out, and_6_out, and_7_out, and_8_out, and_9_out,
       and_10_out, and_11_out, and_12_out, and_13_out, and_14_out, and_15_out, and_16_out, not_1_out,
       not_2_out, not_3_out;

  not not_1 (not_1_out, w);
  not not_2 (not_2_out, x);
  not not_3 (not_3_out, y);
  and and_1 (and_1_out, not_1_out, not_2_out);
  and and_2 (and_2_out, w, x);
  and and_3 (and_3_out, not_1_out, not_3_out);
  and and_4 (and_4_out, w, y);
  and and_5 (and_5_out, not_1_out, not_2_out);
  and and_6 (and_6_out, not_2_out, y);
  and and_7 (and_7_out, not_1_out, y);
  and and_8 (and_8_out, not_3_out, x);
  and and_9 (and_9_out, not_1_out, y);
  and and_10 (and_10_out, not_2_out, y);
  and and_11 (and_11_out, not_1_out, not_3_out);
  or or_1 (e, and_11_out, and_12_out);
  and and_12 (and_12_out, not_1_out, x);
  and and_13 (and_13_out, not_1_out, not_3_out);
  and and_14 (and_14_out, w, not_2_out, y);
  or or_2 (d, and_13_out, and_14_out, z, and_15_out, and_16_out);
  and and_15 (and_15_out, not_3_out, x);
  and and_16 (and_16_out, x, not_1_out);
  or or_3 (c, w, not_2_out, y);
  or or_4 (b, and_1_out, not_3_out, and_2_out);
  or or_5 (a, and_3_out, x, z, and_4_out);
  or or_6 (f, and_5_out, and_6_out, and_7_out, z);
  or or_7 (g, and_8_out, and_9_out, and_10_out, z);
endmodule

module _1bitadder (
  input  CarryIn,
  input  A,
  input  B,
  output Sum,
  output CarryOut
);

  wire and_1_out, and_2_out, and_3_out, and_4_out, and_5_out, and_6_out, and_7_out, not_1_out, not_2_out,
       not_3_out, not_4_out, not_5_out, not_6_out;

  not not_1 (not_1_out, CarryIn);
  not not_2 (not_2_out, A);
  not not_3 (not_3_out, CarryIn);
  not not_4 (not_4_out, B);
  not not_5 (not_5_out, A);
  not not_6 (not_6_out, B);
  and and_1 (and_1_out, A, B);
  and and_2 (and_2_out, CarryIn, B);
  and and_3 (and_3_out, CarryIn, A);
  and and_4 (and_4_out, not_1_out, not_2_out, B);
  and and_5 (and_5_out, not_3_out, A, not_4_out);
  and and_6 (and_6_out, CarryIn, not_5_out, not_6_out);
  and and_7 (and_7_out, CarryIn, A, B);
  or or_1 (CarryOut, and_1_out, and_2_out, and_3_out);
  or or_2 (Sum, and_4_out, and_5_out, and_6_out, and_7_out);
endmodule

module _4bitadder (
  input  Control_Line,
  input  A0,
  input  B0,
  input  A1,
  input  B1,
  input  A2,
  input  B2,
  input  A3,
  input  A3_2,
  output S0,
  output S1,
  output S2,
  output S3,
  output Carry_Out
);

  wire n1bitadder_1_carryout, n1bitadder_2_carryout, n1bitadder_3_carryout, xor_1_out, xor_2_out, xor_3_out,
       xor_4_out;

  xor xor_1 (xor_1_out, Control_Line, B0);
  xor xor_2 (xor_2_out, Control_Line, B1);
  xor xor_3 (xor_3_out, Control_Line, B2);
  xor xor_4 (xor_4_out, Control_Line, A3_2);
  _1bitadder u_1bitadder_1 (.CarryIn(Control_Line), .A(A0), .B(xor_1_out), .Sum(S0), .CarryOut(n1bitadder_1_carryout));
  _1bitadder u_1bitadder_2 (
    .CarryIn(n1bitadder_1_carryout), .A(A1), .B(xor_2_out), .Sum(S1), .CarryOut(n1bitadder_2_carryout));
  _1bitadder u_1bitadder_3 (
    .CarryIn(n1bitadder_2_carryout), .A(A2), .B(xor_3_out), .Sum(S2), .CarryOut(n1bitadder_3_carryout));
  _1bitadder u_1bitadder_4 (.CarryIn(n1bitadder_3_carryout), .A(A3), .B(xor_4_out), .Sum(S3), .CarryOut(Carry_Out));
endmodule

module _4bit_to_out (
  input  in_1,
  input  in_2,
  input  in_3,
  input  in_4,
  output out_5,
  output out_6,
  output out_7,
  output out_8,
  output out_9,
  output out_10,
  output out_11,
  output out_12
);
endmodule

module _4_bit_adder_2 (
  input  A,
  input  B,
  input  Cin,
  output S,
  output Cout
);

  wire and_1_out, and_2_out, and_3_out, and_4_out, and_5_out, and_6_out, and_7_out, and_8_out, and_9_out,
       and_10_out, and_11_out, not_1_out, not_2_out, not_3_out, not_4_out, not_5_out, not_6_out, or_1_out,
       or_3_out, or_4_out;

  not not_1 (not_1_out, A);
  and and_1 (and_1_out, not_1_out, not_2_out);
  not not_2 (not_2_out, B);
  not not_3 (not_3_out, A);
  and and_2 (and_2_out, not_3_out, B);
  not not_4 (not_4_out, Cin);
  and and_3 (and_3_out, A, not_5_out);
  not not_5 (not_5_out, B);
  not not_6 (not_6_out, Cin);
  and and_4 (and_4_out, A, B);
  and and_5 (and_5_out, B, Cin);
  and and_6 (and_6_out, A, Cin);
  and and_7 (and_7_out, and_1_out, Cin);
  and and_8 (and_8_out, and_2_out, not_4_out);
  and and_9 (and_9_out, and_3_out, not_6_out);
  and and_10 (and_10_out, and_4_out, Cin);
  or or_1 (or_1_out, and_5_out, and_6_out);
  or or_2 (Cout, or_1_out, and_11_out);
  and and_11 (and_11_out, A, B);
  or or_3 (or_3_out, and_7_out, and_8_out);
  or or_4 (or_4_out, and_9_out, and_10_out);
  or or_5 (S, or_3_out, or_4_out);
endmodule
