// Logisim project proj_3.circ as structural Verilog: 6 circuits, main circuit main
module main (
  input  x
);

  _7_Segment_Display u_7_segment_display_1 ();  // open: g, f, a, b, e, d, c, dp
  _7_Segment_Display u_7_segment_display_2 ();  // open: g, f, a, b, e, d, c, dp
endmodule

module base_10_up_down_counter (
);

  wire clock_1_out, clock_2_out, j_k_ff_1_q, j_k_ff_1_qn, j_k_ff_2_q, j_k_ff_2_qn, j_k_ff_3_q, j_k_ff_3_qn,
       j_k_ff_4_q, j_k_ff_4_qn, j_k_ff_5_q, j_k_ff_5_qn, j_k_ff_6_qn, j_k_ff_7_q, j_k_ff_7_qn, j_k_ff_8_qn;

  Clock clock_1 (.out(clock_1_out));
  Clock clock_2 (.out(clock_2_out));
  J_K_Flip_Flop j_k_ff_1 (
    .J(1'b1), .clk(clock_1_out), .K(1'b1), .Q(j_k_ff_1_q), .Qn(j_k_ff_1_qn));  // open: preset, en, reset
  J_K_Flip_Flop j_k_ff_2 (
    .J(1'b1), .clk(clock_2_out), .K(1'b1), .Q(j_k_ff_2_q), .Qn(j_k_ff_2_qn));  // open: preset, en, reset
  J_K_Flip_Flop j_k_ff_3 (
    .J(1'b1), .clk(j_k_ff_1_q), .K(1'b1), .Q(j_k_ff_3_q), .Qn(j_k_ff_3_qn));  // open: preset, en, reset
  J_K_Flip_Flop j_k_ff_4 (
    .J(1'b1), .clk(j_k_ff_2_q), .K(1'b1), .Q(j_k_ff_4_q), .Qn(j_k_ff_4_qn));  // open: preset, en, reset
  J_K_Flip_Flop j_k_ff_5 (
    .J(1'b1), .clk(j_k_ff_3_q), .K(1'b1), .Q(j_k_ff_5_q), .Qn(j_k_ff_5_qn));  // open: preset, en, reset
  J_K_Flip_Flop j_k_ff_6 (.J(1'b1), .clk(j_k_ff_5_q), .K(1'b1), .Qn(j_k_ff_6_qn));  // open: Q, preset, en, reset
  J_K_Flip_Flop j_k_ff_7 (
    .J(1'b1), .clk(j_k_ff_4_q), .K(1'b1), .Q(j_k_ff_7_q), .Qn(j_k_ff_7_qn));  // open: preset, en, reset
  // Probe on j_k_ff_6_qn
  // Probe on j_k_ff_5_qn
  // Probe on j_k_ff_3_qn
  // Probe on j_k_ff_1_qn
  J_K_Flip_Flop j_k_ff_8 (.J(1'b1), .clk(j_k_ff_7_q), .K(1'b1), .Qn(j_k_ff_8_qn));  // open: Q, preset, en, reset
  // Probe on j_k_ff_2_qn
  // Probe on j_k_ff_4_qn
  // Probe on j_k_ff_7_qn
  // Probe on j_k_ff_8_qn
endmodule

module base_6_up_down_counter (
  input  in_1,
  input  in_2,
  input  in_3,
  input  x
);

  wire and_1_out, clock_1_out;

  Clock clock_1 (.out(clock_1_out));
  J_K_Flip_Flop j_k_ff_1 (.J(x), .clk(clock_1_out), .K(x), .Q(in_1));  // open: Qn, preset, en, reset
  J_K_Flip_Flop j_k_ff_2 (.J(in_1), .clk(clock_1_out), .K(in_1), .Q(in_2));  // open: Qn, preset, en, reset
  and and_1 (and_1_out, in_1, in_2);
  J_K_Flip_Flop j_k_ff_3 (.J(and_1_out), .clk(clock_1_out), .K(and_1_out), .Q(in_3));  // open: Qn, preset, en, reset
endmodule

module base_6_up_down_counter2 (
  output out_1,
  output out_2,
  output out_3
);

  wire and_1_out, clock_1_out;

  Clock clock_1 (.out(clock_1_out));
  T_Flip_Flop t_ff_1 (.clk(clock_1_out), .T(1'b1), .Q(out_3));  // open: Qn, preset, reset, en
  T_Flip_Flop t_ff_2 (.clk(clock_1_out), .T(out_3), .Q(out_2));  // open: Qn, preset, reset, en
  and and_1 (and_1_out, out_2, out_3);
  T_Flip_Flop t_ff_3 (.clk(clock_1_out), .T(and_1_out), .Q(out_1));  // open: Qn, preset, reset, en
endmodule

module base10updowncounter2 (
  input  in_1,
  output out_2,
  output out_3,
  output out_4,
  output out_5
);

  wire and_1_out, and_2_out, and_3_out, and_4_out, and_5_out, and_6_out, button_1_out, clock_1_out,
       d_ff_1_qn, d_ff_2_qn, d_ff_3_qn, not_1_out, or_1_out, or_2_out, or_3_out, or_4_out, xor_1_out,
       xor_2_out, xor_3_out, xor_4_out;

  and and_1 (and_1_out, in_1, d_ff_1_qn);
  and and_2 (and_2_out, and_1_out, d_ff_2_qn);
  and and_3 (and_3_out, and_2_out, d_ff_3_qn);
  not not_1 (not_1_out, in_1);
  and and_4 (and_4_out, in_1, out_2);
  and and_5 (and_5_out, and_4_out, out_3);
  and and_6 (and_6_out, and_5_out, out_4);
  or or_1 (or_1_out, in_1, not_1_out);
  or or_2 (or_2_out, and_4_out, and_1_out);
  or or_3 (or_3_out, and_5_out, and_2_out);
  or or_4 (or_4_out, and_6_out, and_3_out);
  xor xor_1 (xor_1_out, out_2, or_1_out);
  xor xor_2 (xor_2_out, out_3, or_2_out);
  xor xor_3 (xor_3_out, out_4, or_3_out);
  xor xor_4 (xor_4_out, out_5, or_4_out);
  Clock clock_1 (.out(clock_1_out));
  D_Flip_Flop #(.trigger("falling")) d_ff_1 (
    .clk(clock_1_out), .D(xor_1_out), .Q(out_2), .Qn(d_ff_1_qn), .reset(button_1_out));  // open: preset, en
  D_Flip_Flop #(.trigger("falling")) d_ff_2 (
    .clk(clock_1_out), .D(xor_2_out), .Q(out_3), .Qn(d_ff_2_qn), .reset(button_1_out));  // open: preset, en
  D_Flip_Flop #(.trigger("falling")) d_ff_3 (
    .clk(clock_1_out), .D(xor_3_out), .Q(out_4), .Qn(d_ff_3_qn), .reset(button_1_out));  // open: preset, en
  D_Flip_Flop #(.trigger("falling")) d_ff_4 (
    .clk(clock_1_out), .D(xor_4_out), .Q(out_5), .reset(button_1_out));  // open: Qn, preset, en
  Button button_1 (.out(button_1_out));
endmodule

module base10counter3 (
  input  in_1,
  output out_2,
  output out_3,
  output out_4,
  output out_5
);

  wire and_1_out, and_2_out, and_3_out, and_4_out, and_5_out, and_6_out, button_1_out, clock_1_out,
       d_ff_1_qn, d_ff_2_qn, d_ff_3_qn, not_1_out, or_1_out, or_2_out, or_3_out, or_4_out, xor_1_out,
       xor_2_out, xor_3_out, xor_4_out;

  not not_1 (not_1_out, in_1);
  and and_1 (and_1_out, not_1_out, d_ff_1_qn);
  and and_2 (and_2_out, and_1_out, d_ff_2_qn);
  and and_3 (and_3_out, and_2_out, d_ff_3_qn);
  and and_4 (and_4_out, in_1, out_2);
  and and_5 (and_5_out, and_4_out, out_3);
  and and_6 (and_6_out, and_5_out, out_4);
  or or_1 (or_1_out, in_1, not_1_out);
  or or_2 (or_2_out, and_4_out, and_1_out);
  or or_3 (or_3_out, and_5_out, and_2_out);
  or or_4 (or_4_out, and_6_out, and_3_out);
  xor xor_1 (xor_1_out, out_2, or_1_out);
  xor xor_2 (xor_2_out, out_3, or_2_out);
  xor xor_3 (xor_3_out, out_4, or_3_out);
  xor xor_4 (xor_4_out, out_5, or_4_out);
  Clock clock_1 (.out(clock_1_out));
  D_Flip_Flop #(.trigger("falling")) d_ff_1 (
    .clk(clock_1_out), .D(xor_1_out), .Q(out_2), .Qn(d_ff_1_qn), .reset(button_1_out));  // open: preset, en
  D_Flip_Flop #(.trigger("falling")) d_ff_2 (
    .clk(clock_1_out), .D(xor_2_out), .Q(out_3), .Qn(d_ff_2_qn), .reset(button_1_out));  // open: preset, en
  D_Flip_Flop #(.trigger("falling")) d_ff_3 (
    .clk(clock_1_out), .D(xor_3_out), .Q(out_4), .Qn(d_ff_3_qn), .reset(button_1_out));  // open: preset, en
  D_Flip_Flop #(.trigger("falling")) d_ff_4 (
    .clk(clock_1_out), .D(xor_4_out), .Q(out_5), .reset(button_1_out));  // open: Qn, preset, en
  Button button_1 (.out(button_1_out));
endmodule
